// Logisim project 实验5.circ as structural Verilog: 16 circuits, main circuit 四位二进制可逆计数器
module \四位二进制可逆计数器  (
  input  CPD,
  input  CPU,
  input  CLR,
  input  in_4,
  output QA,
  output out_6,
  output QB,
  output QC,
  output QD,
  output out_10
);

  wire and_1_out, and_2_out, and_3_out, and_4_out, and_5_out, and_6_out, and_7_out, and_9_out, and_10_out,
       and_11_out, and_12_out, and_13_out, and_14_out, and_15_out, and_16_out, D1_qn, D2_qn, D3_qn, D4_qn,
       not_1_out, not_2_out, not_3_out, not_4_out, not_5_out, not_6_out, not_7_out, not_8_out, or_1_out,
       or_2_out, or_3_out, or_4_out, or_5_out, or_6_out, or_7_out, or_8_out;

  not not_1 (not_1_out, out_6);
  and and_1 (and_1_out, CPD, not_1_out);
  or or_1 (or_1_out, and_1_out, CPU);
  and and_2 (and_2_out, D1_qn, and_1_out);
  and and_3 (and_3_out, QA, CPU);
  and and_4 (and_4_out, D1_qn, D2_qn, and_1_out);
  and and_5 (and_5_out, QA, QB, CPU);
  and and_6 (and_6_out, D1_qn, D2_qn, D3_qn, and_1_out);
  and and_7 (and_7_out, QA, QB, QC, CPU);
  or or_2 (or_2_out, and_2_out, and_3_out);
  or or_3 (or_3_out, and_4_out, and_5_out);
  or or_4 (or_4_out, and_6_out, and_7_out);
  nor nor_1 (out_6, QA, QB, QC, QD);
  D_Flip_Flop #(.trigger("falling"), .Pre_Clr_Positions("LEGACY"), .NegatePresetClear("false"), .enable("true"), .NewFFLayout("false")) D1 (
    .clk(or_1_out), .D(D1_qn), .Q(QA), .Qn(D1_qn), .preset(and_9_out), .en(in_4), .reset(or_5_out));
  or or_5 (or_5_out, and_10_out, CLR);
  D_Flip_Flop #(.trigger("falling"), .Pre_Clr_Positions("LEGACY"), .NegatePresetClear("false"), .enable("true"), .NewFFLayout("false")) D2 (
    .clk(or_2_out), .D(D2_qn), .Q(QB), .Qn(D2_qn), .preset(and_11_out), .en(in_4), .reset(or_6_out));
  or or_6 (or_6_out, and_12_out, CLR);
  D_Flip_Flop #(.trigger("falling"), .Pre_Clr_Positions("LEGACY"), .NegatePresetClear("false"), .enable("true"), .NewFFLayout("false")) D3 (
    .clk(or_3_out), .D(D3_qn), .Q(QC), .Qn(D3_qn), .preset(and_13_out), .en(in_4), .reset(or_7_out));
  or or_7 (or_7_out, and_14_out, CLR);
  D_Flip_Flop #(.trigger("falling"), .Pre_Clr_Positions("LEGACY"), .NegatePresetClear("false"), .enable("true"), .NewFFLayout("false")) D4 (
    .clk(or_4_out), .D(D4_qn), .Q(QD), .Qn(D4_qn), .preset(and_15_out), .en(in_4), .reset(or_8_out));
  or or_8 (or_8_out, and_16_out, CLR);
  not not_2 (not_2_out, QC);
  and and_8 (out_10, QD, not_2_out, QB, not_3_out);
  not not_3 (not_3_out, QA);
  and and_9 (and_9_out, not_8_out, 1'b1);
  and and_10 (and_10_out, not_4_out, not_8_out);
  and and_11 (and_11_out, 1'b0, not_8_out);
  and and_12 (and_12_out, not_5_out, not_8_out);
  and and_13 (and_13_out, 1'b0, not_8_out);
  and and_14 (and_14_out, not_6_out, not_8_out);
  and and_15 (and_15_out, 1'b1, not_8_out);
  and and_16 (and_16_out, not_7_out, not_8_out);
  not not_4 (not_4_out, 1'b1);
  not not_5 (not_5_out, 1'b0);
  not not_6 (not_6_out, 1'b0);
  not not_7 (not_7_out, 1'b1);
  not not_8 (not_8_out, in_4);
endmodule

module \四位二进制可逆计数器2  (
  input  CPD,
  input  CPU,
  input  CLR,
  input  in_4,
  input  in_5,
  output QA,
  output QB,
  output out_8,
  output QC,
  output QD,
  output out_11
);

  wire and_1_out, and_2_out, and_3_out, and_4_out, and_5_out, and_6_out, and_7_out, and_9_out, and_10_out,
       and_11_out, and_12_out, and_13_out, and_14_out, and_15_out, and_16_out, D1_qn, D2_qn, D3_qn, D4_qn,
       multiplexer_1_out, not_1_out, not_2_out, not_3_out, not_4_out, not_5_out, not_6_out, not_7_out,
       not_8_out, or_1_out, or_2_out, or_3_out, or_4_out, or_5_out, or_6_out, or_7_out, or_8_out;

  not not_1 (not_1_out, out_8);
  and and_1 (and_1_out, CPD, not_1_out);
  or or_1 (or_1_out, and_1_out, CPU);
  and and_2 (and_2_out, D1_qn, and_1_out);
  and and_3 (and_3_out, QA, CPU);
  and and_4 (and_4_out, D1_qn, D2_qn, and_1_out);
  and and_5 (and_5_out, QA, QB, CPU);
  and and_6 (and_6_out, D1_qn, D2_qn, D3_qn, and_1_out);
  and and_7 (and_7_out, QA, QB, QC, CPU);
  or or_2 (or_2_out, and_2_out, and_3_out);
  or or_3 (or_3_out, and_4_out, and_5_out);
  or or_4 (or_4_out, and_6_out, and_7_out);
  nor nor_1 (out_8, QD, QC, QB, QA);
  D_Flip_Flop #(.trigger("falling"), .Pre_Clr_Positions("LEGACY"), .NegatePresetClear("false"), .enable("true"), .NewFFLayout("false")) D1 (
    .clk(or_1_out), .D(D1_qn), .Q(QA), .Qn(D1_qn), .preset(and_9_out), .en(in_4), .reset(or_5_out));
  D_Flip_Flop #(.trigger("falling"), .Pre_Clr_Positions("LEGACY"), .NegatePresetClear("false"), .enable("true"), .NewFFLayout("false")) D2 (
    .clk(or_2_out), .D(D2_qn), .Q(QB), .Qn(D2_qn), .preset(and_11_out), .en(in_4), .reset(or_6_out));
  D_Flip_Flop #(.trigger("falling"), .Pre_Clr_Positions("LEGACY"), .NegatePresetClear("false"), .enable("true"), .NewFFLayout("false")) D3 (
    .clk(or_3_out), .D(D3_qn), .Q(QC), .Qn(D3_qn), .preset(and_13_out), .en(in_4), .reset(or_7_out));
  D_Flip_Flop #(.trigger("falling"), .Pre_Clr_Positions("LEGACY"), .NegatePresetClear("false"), .enable("true"), .NewFFLayout("false")) D4 (
    .clk(or_4_out), .D(D4_qn), .Q(QD), .Qn(D4_qn), .preset(and_15_out), .en(in_4), .reset(or_8_out));
  or or_5 (or_5_out, and_10_out, CLR);
  or or_6 (or_6_out, and_12_out, CLR);
  or or_7 (or_7_out, and_14_out, CLR);
  or or_8 (or_8_out, and_16_out, CLR);
  not not_2 (not_2_out, QA);
  not not_3 (not_3_out, QC);
  and and_8 (out_11, QD, not_3_out, QB, not_2_out);
  and and_9 (and_9_out, not_8_out, 1'b1);
  and and_10 (and_10_out, not_4_out, not_8_out);
  and and_11 (and_11_out, 1'b0, not_8_out);
  and and_12 (and_12_out, not_5_out, not_8_out);
  and and_13 (and_13_out, 1'b0, not_8_out);
  and and_14 (and_14_out, not_6_out, not_8_out);
  and and_15 (and_15_out, multiplexer_1_out, not_8_out);
  and and_16 (and_16_out, not_7_out, not_8_out);
  not not_4 (not_4_out, 1'b1);
  not not_5 (not_5_out, 1'b0);
  not not_6 (not_6_out, 1'b0);
  not not_7 (not_7_out, multiplexer_1_out);
  not not_8 (not_8_out, in_4);
  Multiplexer #(.select(1), .width(1), .disabled("Z"), .enable("false")) multiplexer_1 (
    .in0(1'b0), .in1(1'b1), .out(multiplexer_1_out), .sel(in_5));
endmodule

module \六十进制计数器  (
  input  Clr,
  input  CPU,
  input  CPD,
  input  Adj,
  output out_5,
  output out_6,
  output out_7,
  output out_8,
  output out_9,
  output out_10,
  output out_11,
  output out_12,
  output out_13
);

  wire and_2_out, and_3_out, and_4_out, nand_1_out, not_1_out, not_2_out, or_1_out, or_2_out,
       \四位二进制可逆计数器_1_out_6 , \四位二进制可逆计数器_2_out_6 , \四位二进制可逆计数器_2_out_10 ;

  and and_1 (out_13, out_6, out_7);
  or or_1 (or_1_out, out_13, Clr);
  and and_2 (and_2_out, and_3_out, \四位二进制可逆计数器_2_out_6 );
  \四位二进制可逆计数器  \u_四位二进制可逆计数器_1  (
    .CPD(and_2_out), .CPU(\四位二进制可逆计数器_2_out_10 ), .QA(out_8), .CLR(or_1_out), .QB(out_7), .QC(out_6),
    .QD(out_5), .out_6(\四位二进制可逆计数器_1_out_6 ));  // open: out_10, in_4
  nand nand_1 (nand_1_out, \四位二进制可逆计数器_1_out_6 , \四位二进制可逆计数器_2_out_6 );
  and and_3 (and_3_out, CPD, nand_1_out, Adj);
  or or_2 (or_2_out, Clr, \四位二进制可逆计数器_2_out_10 );
  and and_4 (and_4_out, and_2_out, not_1_out);
  not not_1 (not_1_out, CPD);
  \四位二进制可逆计数器  \u_四位二进制可逆计数器_2  (
    .CPD(and_3_out), .CPU(CPU), .QA(out_12), .CLR(or_2_out), .QB(out_11), .QC(out_10), .QD(out_9),
    .out_10(\四位二进制可逆计数器_2_out_10 ), .in_4(not_2_out), .out_6(\四位二进制可逆计数器_2_out_6 ));
  not not_2 (not_2_out, and_4_out);
endmodule

module \六十进制计数器测试电路  (
  input  in_1,
  input  in_2,
  input  in_3,
  input  in_4,
  output out_5,
  output out_6,
  output out_7,
  output out_8
);

  wire \六十进制计数器_1_out_13 ;
  wire [3:0] \六十进制计数器_1_out_8 , \六十进制计数器_1_out_12 ;

  Hex_Digit_Display hex_digit_display_1 (.value(\六十进制计数器_1_out_8 ));  // open: dp
  \六十进制计数器  \u_六十进制计数器_1  (
    .Clr(in_3), .CPD(in_4), .Adj(in_2), .out_5(\六十进制计数器_1_out_8 [3]), .out_6(\六十进制计数器_1_out_8 [2]),
    .out_7(\六十进制计数器_1_out_8 [1]), .out_8(\六十进制计数器_1_out_8 [0]), .out_9(\六十进制计数器_1_out_12 [3]),
    .out_10(\六十进制计数器_1_out_12 [2]), .out_11(\六十进制计数器_1_out_12 [1]), .out_12(\六十进制计数器_1_out_12 [0]),
    .CPU(in_1), .out_13(\六十进制计数器_1_out_13 ));
  Hex_Digit_Display hex_digit_display_2 (.value(\六十进制计数器_1_out_12 ));  // open: dp
  \四位二进制可逆计数器  \u_四位二进制可逆计数器_1  (
    .CPD(1'b0), .CPU(\六十进制计数器_1_out_13 ), .QA(out_8), .CLR(in_3), .QB(out_7), .QC(out_6), .QD(out_5));  // open: out_10, in_4, out_6
endmodule

module \十二进制计数器或二十四进制的计数器电路  (
  input  in_1,
  input  SET,
  input  Clr,
  input  CPU,
  input  CPD,
  input  Adj,
  output out_7,
  output out_8,
  output out_9,
  output out_10,
  output out_11,
  output out_12,
  output out_13,
  output out_14,
  output out_15
);

  wire and_1_out, and_2_out, and_3_out, and_4_out, and_5_out, and_6_out, and_7_out, and_8_out, and_9_out,
       and_10_out, and_11_out, and_12_out, and_13_out, buffer_1_out, comparator_1_eq, comparator_2_eq,
       comparator_3_eq, comparator_4_eq, multiplexer_4_out, nand_1_out, not_1_out, not_2_out, not_3_out,
       not_4_out, not_5_out, not_6_out, not_7_out, or_2_out, or_3_out, \四位二进制可逆计数器2_1_out_8 ,
       \四位二进制可逆计数器2_1_out_11 , \四位二进制可逆计数器_1_out_6 ;
  wire [7:0] adder_1_out, multiplexer_1_out, multiplexer_2_out, \四位二进制可逆计数器2_1_qa , \转换1_1_out_2 ;

  and and_1 (and_1_out, not_1_out, CPU, comparator_1_eq);
  or or_1 (out_15, and_1_out, and_3_out);
  Comparator #(.width(8), .mode("twosComplement")) comparator_1 (
    .a(8'h11), .b({out_7, out_8, out_9, out_10, out_11, out_12, out_13, out_14}), .eq(comparator_1_eq));  // open: gt, lt
  not not_1 (not_1_out, SET);
  and and_2 (and_2_out, not_1_out, out_10, out_13, buffer_1_out);
  and and_3 (and_3_out, out_12, SET, out_9);
  or or_2 (or_2_out, and_3_out, and_2_out, Clr);
  and and_4 (and_4_out, comparator_2_eq, and_7_out);
  not not_2 (not_2_out, in_1);
  and and_5 (and_5_out, and_9_out, \四位二进制可逆计数器2_1_out_8 );
  and and_6 (and_6_out, in_1, SET);
  and and_7 (and_7_out, not_2_out, SET);
  not not_3 (not_3_out, comparator_2_eq);
  \四位二进制可逆计数器  \u_四位二进制可逆计数器_1  (
    .CPD(and_5_out), .CPU(\四位二进制可逆计数器2_1_out_11 ), .QA(\四位二进制可逆计数器2_1_qa [4]), .CLR(or_2_out),
    .QB(\四位二进制可逆计数器2_1_qa [5]), .QC(\四位二进制可逆计数器2_1_qa [6]), .QD(\四位二进制可逆计数器2_1_qa [7]),
    .out_6(\四位二进制可逆计数器_1_out_6 ));  // open: out_10, in_4
  nand nand_1 (nand_1_out, \四位二进制可逆计数器_1_out_6 , \四位二进制可逆计数器2_1_out_8 );
  and and_8 (and_8_out, and_6_out, not_3_out);
  Comparator #(.width(8), .mode("twosComplement")) comparator_2 (
    .a(\四位二进制可逆计数器2_1_qa ), .b(8'h12), .eq(comparator_2_eq));  // open: gt, lt
  Multiplexer #(.select(1), .width(8), .disabled("Z"), .enable("false")) multiplexer_1 (
    .in0(multiplexer_2_out), .in1({8{1'b0}}), .out(multiplexer_1_out), .sel(and_4_out));
  Multiplexer #(.select(1), .width(8), .disabled("Z"), .enable("false")) multiplexer_2 (
    .in0(\四位二进制可逆计数器2_1_qa ), .in1(\转换1_1_out_2 ), .out(multiplexer_2_out), .sel(and_8_out));
  Adder #(.width(8)) adder_1 (.a(\四位二进制可逆计数器2_1_qa ), .b(8'h12), .out(adder_1_out));  // open: cin, cout
  and and_9 (and_9_out, CPD, nand_1_out, Adj);
  and and_10 (and_10_out, and_2_out, comparator_3_eq);
  Comparator #(.width(8), .mode("twosComplement")) comparator_3 (
    .a(8'h12), .b({out_7, out_8, out_9, out_10, out_11, out_12, out_13, out_14}), .eq(comparator_3_eq));  // open: gt, lt
  buf buffer_1 (buffer_1_out, out_14);
  Multiplexer #(.select(1), .width(8), .disabled("Z"), .enable("false")) multiplexer_3 (
    .in0(multiplexer_1_out), .in1(8'h12),
    .out({out_7, out_8, out_9, out_10, out_11, out_12, out_13, out_14}), .sel(and_13_out));
  \转换1  \u_转换1_1  (.in_1(adder_1_out), .out_2(\转换1_1_out_2 ));
  or or_3 (or_3_out, Clr, \四位二进制可逆计数器2_1_out_11 );
  Multiplexer #(.select(1), .width(1), .disabled("Z"), .enable("false")) multiplexer_4 (
    .in0(1'b0), .in1(1'b1), .out(multiplexer_4_out), .sel(not_4_out));
  not not_4 (not_4_out, and_10_out);
  not not_5 (not_5_out, CPD);
  and and_11 (and_11_out, and_5_out, not_5_out);
  \四位二进制可逆计数器2  \u_四位二进制可逆计数器2_1  (
    .CPD(and_9_out), .CPU(CPU), .QA(\四位二进制可逆计数器2_1_qa [0]), .CLR(or_3_out), .QB(\四位二进制可逆计数器2_1_qa [1]),
    .in_4(and_12_out), .QC(\四位二进制可逆计数器2_1_qa [2]), .QD(\四位二进制可逆计数器2_1_qa [3]),
    .out_11(\四位二进制可逆计数器2_1_out_11 ), .out_8(\四位二进制可逆计数器2_1_out_8 ), .in_5(multiplexer_4_out));
  and and_12 (and_12_out, not_6_out, multiplexer_4_out);
  not not_6 (not_6_out, and_11_out);
  not not_7 (not_7_out, in_1);
  Comparator #(.width(8), .mode("twosComplement")) comparator_4 (
    .a({8{1'b0}}), .b(\四位二进制可逆计数器2_1_qa ), .eq(comparator_4_eq));  // open: gt, lt
  and and_13 (and_13_out, comparator_4_eq, not_7_out, not_1_out);
endmodule

module \十二进制计数器或二十四进制的计数器测试电路  (
  input  in_1,
  input  in_2,
  input  in_3,
  input  in_4,
  output out_5
);

  wire clock_1_out, not_1_out, \十二进制计数器或二十四进制的计数器电路_1_out_15 , \四位二进制可逆计数器_1_qa ;
  wire [3:0] \十二进制计数器或二十四进制的计数器电路_1_out_10 , \十二进制计数器或二十四进制的计数器电路_1_out_14 ;
  wire [6:0] \上下午文字显示电路_1_out_3 , \上下午文字显示电路_1_out_4 , \上下午文字显示电路_1_out_5 , \上下午文字显示电路_1_out_6 ;

  Clock #(.highDuration(1), .lowDuration(1)) clock_1 (.out(clock_1_out));
  Hex_Digit_Display hex_digit_display_1 (.value(\十二进制计数器或二十四进制的计数器电路_1_out_10 ));  // open: dp
  Hex_Digit_Display hex_digit_display_2 (.value(\十二进制计数器或二十四进制的计数器电路_1_out_14 ));  // open: dp
  \十二进制计数器或二十四进制的计数器电路  \u_十二进制计数器或二十四进制的计数器电路_1  (
    .Clr(in_4), .CPD(in_3), .Adj(in_1), .out_7(\十二进制计数器或二十四进制的计数器电路_1_out_10 [3]),
    .out_8(\十二进制计数器或二十四进制的计数器电路_1_out_10 [2]), .out_9(\十二进制计数器或二十四进制的计数器电路_1_out_10 [1]),
    .out_10(\十二进制计数器或二十四进制的计数器电路_1_out_10 [0]), .out_11(\十二进制计数器或二十四进制的计数器电路_1_out_14 [3]),
    .out_12(\十二进制计数器或二十四进制的计数器电路_1_out_14 [2]), .out_13(\十二进制计数器或二十四进制的计数器电路_1_out_14 [1]),
    .out_14(\十二进制计数器或二十四进制的计数器电路_1_out_14 [0]), .SET(in_2), .out_15(\十二进制计数器或二十四进制的计数器电路_1_out_15 ),
    .CPU(clock_1_out), .in_1(\四位二进制可逆计数器_1_qa ));
  \四位二进制可逆计数器  \u_四位二进制可逆计数器_1  (
    .CPU(\十二进制计数器或二十四进制的计数器电路_1_out_15 ), .QA(\四位二进制可逆计数器_1_qa ), .CLR(out_5), .QB(out_5));  // open: CPD, QC, QD, out_10, in_4, out_6
  DotMatrix #(.inputtype("column"), .matrixcols(5), .matrixrows(7), .persist(0), .dotshape("square")) dotmatrix_1 (
    .col0(\上下午文字显示电路_1_out_3 ), .col1(\上下午文字显示电路_1_out_4 ), .col2(\上下午文字显示电路_1_out_5 ),
    .col3(\上下午文字显示电路_1_out_6 ), .col4(\上下午文字显示电路_1_out_6 ));
  \上下午文字显示电路  \u_上下午文字显示电路_1  (
    .out_3(\上下午文字显示电路_1_out_3 ), .out_4(\上下午文字显示电路_1_out_4 ), .out_5(\上下午文字显示电路_1_out_5 ),
    .out_6(\上下午文字显示电路_1_out_6 ), .AM_FM(\四位二进制可逆计数器_1_qa ), .TT(not_1_out));
  not not_1 (not_1_out, in_2);
endmodule

module \上下午文字显示电路  (
  input  TT,
  input  AM_FM,
  output [6:0] out_3,
  output [6:0] out_4,
  output [6:0] out_5,
  output [6:0] out_6
);

  wire [27:0] multiplexer_1_out;

  Multiplexer #(.select(1), .width(28), .disabled("Z"), .enable("false")) multiplexer_1 (
    .in0(28'h207f89), .in1(28'h8103fc8), .out(multiplexer_1_out), .sel(AM_FM));
  Multiplexer #(.select(1), .width(28), .disabled("Z"), .enable("false")) multiplexer_2 (
    .in0({28{1'b0}}), .in1(multiplexer_1_out), .out({out_3, out_4, out_5, out_6}), .sel(TT));
endmodule

module \上下午文字显示测试电路  (
  input  in_1,
  input  in_2
);

  wire [6:0] \上下午文字显示电路_1_out_3 , \上下午文字显示电路_1_out_4 , \上下午文字显示电路_1_out_5 , \上下午文字显示电路_1_out_6 ;

  DotMatrix #(.inputtype("column"), .matrixcols(5), .matrixrows(7), .persist(0), .dotshape("square")) dotmatrix_1 (
    .col0(\上下午文字显示电路_1_out_3 ), .col1(\上下午文字显示电路_1_out_4 ), .col2(\上下午文字显示电路_1_out_5 ),
    .col3(\上下午文字显示电路_1_out_6 ), .col4(\上下午文字显示电路_1_out_6 ));
  \上下午文字显示电路  \u_上下午文字显示电路_1  (
    .out_3(\上下午文字显示电路_1_out_3 ), .out_4(\上下午文字显示电路_1_out_4 ), .out_5(\上下午文字显示电路_1_out_5 ),
    .out_6(\上下午文字显示电路_1_out_6 ), .AM_FM(in_1), .TT(in_2));
endmodule

module \电子钟整点报时电路  (
  input  in_1,
  input  in_2,
  input  in_3,
  input  in_4,
  input  in_5,
  input  in_6,
  output [3:0] out_7,
  output [3:0] out_8,
  output [3:0] out_9,
  output [3:0] out_10,
  output out_11,
  output [3:0] out_12,
  output [3:0] out_13
);

  wire \六十进制计数器_1_out_13 , \六十进制计数器_2_out_13 ;

  \六十进制计数器  \u_六十进制计数器_1  (
    .Clr(in_6), .CPD(in_4), .Adj(in_5), .out_5(out_7[3]), .out_6(out_7[2]), .out_7(out_7[1]),
    .out_8(out_7[0]), .out_9(out_8[3]), .out_10(out_8[2]), .out_11(out_8[1]), .out_12(out_8[0]), .CPU(in_1),
    .out_13(\六十进制计数器_1_out_13 ));
  \六十进制计数器  \u_六十进制计数器_2  (
    .Clr(in_6), .CPD(in_4), .Adj(in_5), .out_5(out_9[3]), .out_6(out_9[2]), .out_7(out_9[1]),
    .out_8(out_9[0]), .out_9(out_10[3]), .out_10(out_10[2]), .out_11(out_10[1]), .out_12(out_10[0]),
    .CPU(\六十进制计数器_1_out_13 ), .out_13(\六十进制计数器_2_out_13 ));
  and and_1 (out_11, out_7[2], out_7[0], out_9[2], out_9[0], out_10[3], out_10[0]);
  \十二进制计数器或二十四进制的计数器电路  \u_十二进制计数器或二十四进制的计数器电路_1  (
    .Clr(in_6), .CPD(in_4), .Adj(in_5), .out_7(out_12[3]), .out_8(out_12[2]), .out_9(out_12[1]),
    .out_10(out_12[0]), .out_11(out_13[3]), .out_12(out_13[2]), .out_13(out_13[1]), .out_14(out_13[0]),
    .SET(in_2), .CPU(\六十进制计数器_2_out_13 ), .in_1(in_3));  // open: out_15
endmodule

module \电子钟整点报时测试电路  (
  input  in_1,
  input  in_2,
  input  in_3,
  input  in_4,
  input  in_5
);

  wire clock_1_out, \电子钟整点报时电路_1_out_11 ;
  wire [3:0] \电子钟整点报时电路_1_out_7 , \电子钟整点报时电路_1_out_8 , \电子钟整点报时电路_1_out_9 , \电子钟整点报时电路_1_out_10 ,
       \电子钟整点报时电路_1_out_12 , \电子钟整点报时电路_1_out_13 ;

  Clock #(.highDuration(1), .lowDuration(1)) clock_1 (.out(clock_1_out));
  Hex_Digit_Display hex_digit_display_1 (.value(\电子钟整点报时电路_1_out_12 ));  // open: dp
  Hex_Digit_Display hex_digit_display_2 (.value(\电子钟整点报时电路_1_out_13 ));  // open: dp
  Hex_Digit_Display hex_digit_display_3 (.value(\电子钟整点报时电路_1_out_9 ));  // open: dp
  Hex_Digit_Display hex_digit_display_4 (.value(\电子钟整点报时电路_1_out_10 ));  // open: dp
  Hex_Digit_Display hex_digit_display_5 (.value(\电子钟整点报时电路_1_out_7 ));  // open: dp
  \电子钟整点报时电路  \u_电子钟整点报时电路_1  (
    .in_4(in_4), .in_5(in_1), .in_6(in_3), .out_7(\电子钟整点报时电路_1_out_7 ), .out_8(\电子钟整点报时电路_1_out_8 ),
    .out_9(\电子钟整点报时电路_1_out_9 ), .out_10(\电子钟整点报时电路_1_out_10 ), .out_11(\电子钟整点报时电路_1_out_11 ), .in_2(in_2),
    .out_12(\电子钟整点报时电路_1_out_12 ), .out_13(\电子钟整点报时电路_1_out_13 ), .in_1(clock_1_out), .in_3(in_5));
  Hex_Digit_Display hex_digit_display_6 (.value(\电子钟整点报时电路_1_out_8 ));  // open: dp
  LED #(.active("true")) led_1 (.in(\电子钟整点报时电路_1_out_11 ));
endmodule

module \秒脉冲产生电路  (
  input  in_1,
  output out_2
);

  \四位二进制可逆计数器  \u_四位二进制可逆计数器_1  (
    .CPD(1'b0), .CPU(in_1), .CLR(out_2), .QD(out_2));  // open: QA, QB, QC, out_10, in_4, out_6
endmodule

module \闹钟  (
  input  in_1,
  input  in_2,
  input  in_3,
  input  in_4,
  input  in_5,
  input  in_6,
  input  in_7,
  input  in_8,
  output [3:0] out_9,
  output [3:0] out_10,
  output [3:0] out_11,
  output [3:0] out_12,
  output [6:0] out_13,
  output [6:0] out_14,
  output [6:0] out_15,
  output [6:0] out_16,
  output [3:0] out_17,
  output [3:0] out_18,
  output [3:0] out_19,
  output [3:0] out_20,
  output [3:0] out_21,
  output [3:0] out_22,
  output out_23
);

  wire and_2_out, and_3_out, and_4_out, and_5_out, and_6_out, comparator_1_eq, comparator_2_eq,
       multiplexer_1_out, not_1_out, not_2_out, not_3_out, not_4_out, or_1_out, \六十进制计数器_1_out_13 ,
       \六十进制计数器_3_out_13 , \十二进制计数器或二十四进制的计数器电路_2_out_15 , \四位二进制可逆计数器_1_qa , \四位二进制可逆计数器_1_qb ;

  not not_1 (not_1_out, in_7);
  not not_2 (not_2_out, in_2);
  and and_1 (out_23, in_2, not_3_out, comparator_1_eq, multiplexer_1_out);
  and and_2 (and_2_out, in_3, not_2_out);
  Comparator #(.width(16), .mode("twosComplement")) comparator_1 (
    .a({out_12, out_11, out_10, out_9}), .b({out_19, out_20, out_21, out_22}), .eq(comparator_1_eq));  // open: gt, lt
  not not_3 (not_3_out, out_17[0]);
  or or_1 (or_1_out, and_2_out, in_4);
  \六十进制计数器  \u_六十进制计数器_1  (
    .Clr(in_8), .CPD(in_6), .Adj(in_7), .out_5(out_17[3]), .out_6(out_17[2]), .out_7(out_17[1]),
    .out_8(out_17[0]), .out_9(out_18[3]), .out_10(out_18[2]), .out_11(out_18[1]), .out_12(out_18[0]),
    .CPU(or_1_out), .out_13(\六十进制计数器_1_out_13 ));
  and and_3 (and_3_out, in_3, in_7, in_2);
  and and_4 (and_4_out, in_7, in_6, in_2);
  \六十进制计数器  \u_六十进制计数器_2  (
    .CPD(and_4_out), .Adj(1'b1), .out_5(out_12[3]), .out_6(out_12[2]), .out_7(out_12[1]), .out_8(out_12[0]),
    .out_9(out_11[3]), .out_10(out_11[2]), .out_11(out_11[1]), .out_12(out_11[0]), .CPU(and_3_out));  // open: Clr, out_13
  \六十进制计数器  \u_六十进制计数器_3  (
    .Clr(in_8), .CPD(in_6), .Adj(in_7), .out_5(out_19[3]), .out_6(out_19[2]), .out_7(out_19[1]),
    .out_8(out_19[0]), .out_9(out_20[3]), .out_10(out_20[2]), .out_11(out_20[1]), .out_12(out_20[0]),
    .CPU(\六十进制计数器_1_out_13 ), .out_13(\六十进制计数器_3_out_13 ));
  Multiplexer #(.select(1), .width(1), .disabled("Z"), .enable("false")) multiplexer_1 (
    .in0(comparator_2_eq), .in1(1'b1), .out(multiplexer_1_out), .sel(in_5));
  and and_5 (and_5_out, in_3, not_1_out, in_2);
  and and_6 (and_6_out, in_6, not_1_out, in_2);
  \十二进制计数器或二十四进制的计数器电路  \u_十二进制计数器或二十四进制的计数器电路_1  (
    .CPD(and_6_out), .Adj(1'b1), .out_7(out_10[3]), .out_8(out_10[2]), .out_9(out_10[1]), .out_10(out_10[0]),
    .out_11(out_9[3]), .out_12(out_9[2]), .out_13(out_9[1]), .out_14(out_9[0]), .SET(in_5), .CPU(and_5_out),
    .in_1(in_1));  // open: Clr, out_15
  \十二进制计数器或二十四进制的计数器电路  \u_十二进制计数器或二十四进制的计数器电路_2  (
    .Clr(in_8), .CPD(in_6), .Adj(in_7), .out_7(out_21[3]), .out_8(out_21[2]), .out_9(out_21[1]),
    .out_10(out_21[0]), .out_11(out_22[3]), .out_12(out_22[2]), .out_13(out_22[1]), .out_14(out_22[0]),
    .SET(in_5), .out_15(\十二进制计数器或二十四进制的计数器电路_2_out_15 ), .CPU(\六十进制计数器_3_out_13 ), .in_1(\四位二进制可逆计数器_1_qa ));
  Comparator #(.width(1), .mode("twosComplement")) comparator_2 (
    .a(in_1), .b(\四位二进制可逆计数器_1_qa ), .eq(comparator_2_eq));  // open: gt, lt
  \四位二进制可逆计数器  \u_四位二进制可逆计数器_1  (
    .CPD(in_6), .CPU(\十二进制计数器或二十四进制的计数器电路_2_out_15 ), .QA(\四位二进制可逆计数器_1_qa ), .CLR(\四位二进制可逆计数器_1_qb ),
    .QB(\四位二进制可逆计数器_1_qb ));  // open: QC, QD, out_10, in_4, out_6
  \上下午文字显示电路  \u_上下午文字显示电路_1  (
    .out_3(out_16), .out_4(out_13), .out_5(out_14), .out_6(out_15), .AM_FM(\四位二进制可逆计数器_1_qa ), .TT(not_4_out));
  not not_4 (not_4_out, in_5);
endmodule

module \闹钟测试  (
  input  in_1,
  input  in_2,
  input  in_3,
  input  in_4,
  input  in_5,
  input  in_6,
  input  in_7
);

  wire clock_1_out, \闹钟_1_out_23 ;
  wire [3:0] \闹钟_1_out_9 , \闹钟_1_out_10 , \闹钟_1_out_11 , \闹钟_1_out_12 , \闹钟_1_out_17 , \闹钟_1_out_18 ,
       \闹钟_1_out_19 , \闹钟_1_out_20 , \闹钟_1_out_21 , \闹钟_1_out_22 ;
  wire [6:0] \闹钟_1_out_13 , \闹钟_1_out_14 , \闹钟_1_out_15 , \闹钟_1_out_16 ;

  Clock #(.highDuration(1), .lowDuration(1)) clock_1 (.out(clock_1_out));
  Hex_Digit_Display hex_digit_display_1 (.value(\闹钟_1_out_10 ));  // open: dp
  DotMatrix #(.inputtype("column"), .matrixcols(5), .matrixrows(7), .persist(0), .dotshape("square")) dotmatrix_1 (
    .col0(\闹钟_1_out_16 ), .col1(\闹钟_1_out_13 ), .col2(\闹钟_1_out_14 ), .col3(\闹钟_1_out_15 ),
    .col4(\闹钟_1_out_15 ));
  Hex_Digit_Display hex_digit_display_2 (.value(\闹钟_1_out_9 ));  // open: dp
  Hex_Digit_Display hex_digit_display_3 (.value(\闹钟_1_out_21 ));  // open: dp
  Hex_Digit_Display hex_digit_display_4 (.value(\闹钟_1_out_11 ));  // open: dp
  Hex_Digit_Display hex_digit_display_5 (.value(\闹钟_1_out_12 ));  // open: dp
  Hex_Digit_Display hex_digit_display_6 (.value(\闹钟_1_out_22 ));  // open: dp
  \闹钟  \u_闹钟_1  (
    .in_3(in_1), .in_6(in_5), .in_7(in_3), .in_8(in_4), .in_5(in_2), .in_2(in_6), .out_17(\闹钟_1_out_17 ),
    .out_18(\闹钟_1_out_18 ), .out_19(\闹钟_1_out_19 ), .out_20(\闹钟_1_out_20 ), .out_21(\闹钟_1_out_21 ),
    .out_22(\闹钟_1_out_22 ), .out_16(\闹钟_1_out_16 ), .out_13(\闹钟_1_out_13 ), .out_14(\闹钟_1_out_14 ),
    .out_15(\闹钟_1_out_15 ), .out_23(\闹钟_1_out_23 ), .in_1(in_7), .out_12(\闹钟_1_out_12 ),
    .out_11(\闹钟_1_out_11 ), .out_10(\闹钟_1_out_10 ), .out_9(\闹钟_1_out_9 ), .in_4(clock_1_out));
  Hex_Digit_Display hex_digit_display_7 (.value(\闹钟_1_out_20 ));  // open: dp
  Hex_Digit_Display hex_digit_display_8 (.value(\闹钟_1_out_19 ));  // open: dp
  LED #(.active("true")) led_1 (.in(\闹钟_1_out_23 ));
  Hex_Digit_Display hex_digit_display_9 (.value(\闹钟_1_out_17 ));  // open: dp
  Hex_Digit_Display hex_digit_display_10 (.value(\闹钟_1_out_18 ));  // open: dp
endmodule

module \多功能数字钟电路  (
  input  in_1,
  input  cpd,
  input  in_3,
  input  clr,
  input  adj0,
  input  adj1,
  input  cpu,
  output [6:0] out_8,
  output [6:0] out_9,
  output [6:0] out_10,
  output [6:0] out_11,
  output [3:0] out_12,
  output [3:0] out_13,
  output [3:0] out_14,
  output [3:0] out_15,
  output out_16,
  output [3:0] out_17,
  output [3:0] out_18
);

  wire and_1_out, and_2_out, and_3_out, and_5_out, comparator_1_eq, comparator_2_eq, multiplexer_1_out,
       multiplexer_2_out, multiplexer_3_out, multiplexer_4_out, multiplexer_5_out, multiplexer_6_out,
       nor_1_out, not_1_out, not_2_out, not_3_out, or_1_out, \六十进制计数器_1_out_13 , \六十进制计数器_2_out_13 ,
       \十二进制计数器或二十四进制的计数器电路_1_out_15 , \四位二进制可逆计数器_1_qa , \四位二进制可逆计数器_1_qb , \秒脉冲产生电路_1_out_2 ;

  and and_1 (and_1_out, 1'b0, not_1_out, comparator_1_eq, multiplexer_6_out);
  Comparator #(.width(16), .mode("twosComplement")) comparator_1 (
    .a({16{1'b0}}), .b({out_14, out_15, out_17, out_18}), .eq(comparator_1_eq));  // open: gt, lt
  not not_1 (not_1_out, out_12[0]);
  \秒脉冲产生电路  \u_秒脉冲产生电路_1  (.in_1(in_1), .out_2(\秒脉冲产生电路_1_out_2 ));
  and and_2 (and_2_out, adj0, adj1);
  not not_2 (not_2_out, adj1);
  \六十进制计数器  \u_六十进制计数器_1  (
    .Clr(clr), .CPD(1'b0), .Adj(1'b0), .out_5(out_12[3]), .out_6(out_12[2]), .out_7(out_12[1]),
    .out_8(out_12[0]), .out_9(out_13[3]), .out_10(out_13[2]), .out_11(out_13[1]), .out_12(out_13[0]),
    .CPU(\秒脉冲产生电路_1_out_2 ), .out_13(\六十进制计数器_1_out_13 ));
  and and_3 (and_3_out, adj0, not_2_out);
  Multiplexer #(.select(1), .width(1), .disabled("Z"), .enable("false")) multiplexer_1 (
    .in0(1'b0), .in1(cpd), .out(multiplexer_1_out), .sel(and_2_out));
  \六十进制计数器  \u_六十进制计数器_2  (
    .Clr(clr), .CPD(multiplexer_1_out), .Adj(and_2_out), .out_5(out_14[3]), .out_6(out_14[2]),
    .out_7(out_14[1]), .out_8(out_14[0]), .out_9(out_15[3]), .out_10(out_15[2]), .out_11(out_15[1]),
    .out_12(out_15[0]), .CPU(multiplexer_2_out), .out_13(\六十进制计数器_2_out_13 ));
  Multiplexer #(.select(1), .width(1), .disabled("Z"), .enable("false")) multiplexer_2 (
    .in0(\六十进制计数器_1_out_13 ), .in1(cpu), .out(multiplexer_2_out), .sel(and_2_out));
  and and_4 (out_16, out_12[2], out_12[0], out_14[2], out_14[0], out_15[3], out_15[0]);
  Multiplexer #(.select(1), .width(1), .disabled("Z"), .enable("false")) multiplexer_3 (
    .in0(\六十进制计数器_2_out_13 ), .in1(1'b0), .out(multiplexer_3_out), .sel(and_2_out));
  Multiplexer #(.select(1), .width(1), .disabled("Z"), .enable("false")) multiplexer_4 (
    .in0(multiplexer_3_out), .in1(cpu), .out(multiplexer_4_out), .sel(and_3_out));
  Multiplexer #(.select(1), .width(1), .disabled("Z"), .enable("false")) multiplexer_5 (
    .in0(1'b0), .in1(cpd), .out(multiplexer_5_out), .sel(and_3_out));
  Multiplexer #(.select(1), .width(1), .disabled("Z"), .enable("false")) multiplexer_6 (
    .in0(comparator_2_eq), .in1(1'b1), .out(multiplexer_6_out), .sel(in_3));
  \十二进制计数器或二十四进制的计数器电路  \u_十二进制计数器或二十四进制的计数器电路_1  (
    .Clr(clr), .CPD(multiplexer_5_out), .Adj(and_3_out), .out_7(out_17[3]), .out_8(out_17[2]),
    .out_9(out_17[1]), .out_10(out_17[0]), .out_11(out_18[3]), .out_12(out_18[2]), .out_13(out_18[1]),
    .out_14(out_18[0]), .SET(in_3), .out_15(\十二进制计数器或二十四进制的计数器电路_1_out_15 ), .CPU(multiplexer_4_out),
    .in_1(\四位二进制可逆计数器_1_qa ));
  nor nor_1 (nor_1_out, out_17[3], out_17[2], out_17[1], out_17[0], out_18[0], out_18[1], out_18[2], out_18[3]);
  Comparator #(.width(1), .mode("twosComplement")) comparator_2 (
    .a(1'b0), .b(\四位二进制可逆计数器_1_qa ), .eq(comparator_2_eq));  // open: gt, lt
  or or_1 (or_1_out, \四位二进制可逆计数器_1_qb , clr);
  and and_5 (and_5_out, cpd, nor_1_out);
  \四位二进制可逆计数器  \u_四位二进制可逆计数器_1  (
    .CPD(and_5_out), .CPU(\十二进制计数器或二十四进制的计数器电路_1_out_15 ), .QA(\四位二进制可逆计数器_1_qa ), .CLR(or_1_out),
    .QB(\四位二进制可逆计数器_1_qb ));  // open: QC, QD, out_10, in_4, out_6
  \上下午文字显示电路  \u_上下午文字显示电路_1  (
    .out_3(out_11), .out_4(out_8), .out_5(out_9), .out_6(out_10), .AM_FM(\四位二进制可逆计数器_1_qa ), .TT(not_3_out));
  not not_3 (not_3_out, in_3);
  // also tied to GND on the sheet: and_1_out
endmodule

module \多功能数字钟测试电路  (
  input  in_1,
  input  in_2,
  input  in_3,
  input  in_4,
  input  in_5,
  input  in_6
);

  wire clock_1_out, \多功能数字钟电路_1_out_16 ;
  wire [3:0] \多功能数字钟电路_1_out_12 , \多功能数字钟电路_1_out_13 , \多功能数字钟电路_1_out_14 , \多功能数字钟电路_1_out_15 ,
       \多功能数字钟电路_1_out_17 , \多功能数字钟电路_1_out_18 ;
  wire [6:0] \多功能数字钟电路_1_out_8 , \多功能数字钟电路_1_out_9 , \多功能数字钟电路_1_out_10 , \多功能数字钟电路_1_out_11 ;

  DotMatrix #(.inputtype("column"), .matrixcols(5), .matrixrows(7), .persist(0), .dotshape("square")) dotmatrix_1 (
    .col0(\多功能数字钟电路_1_out_11 ), .col1(\多功能数字钟电路_1_out_8 ), .col2(\多功能数字钟电路_1_out_9 ),
    .col3(\多功能数字钟电路_1_out_10 ), .col4(\多功能数字钟电路_1_out_10 ));
  Clock #(.highDuration(1), .lowDuration(1)) clock_1 (.out(clock_1_out));
  Hex_Digit_Display hex_digit_display_1 (.value(\多功能数字钟电路_1_out_17 ));  // open: dp
  Hex_Digit_Display hex_digit_display_2 (.value(\多功能数字钟电路_1_out_18 ));  // open: dp
  Hex_Digit_Display hex_digit_display_3 (.value(\多功能数字钟电路_1_out_14 ));  // open: dp
  Hex_Digit_Display hex_digit_display_4 (.value(\多功能数字钟电路_1_out_15 ));  // open: dp
  \多功能数字钟电路  \u_多功能数字钟电路_1  (
    .cpu(in_3), .cpd(in_4), .clr(in_6), .adj0(in_1), .adj1(in_2), .out_16(\多功能数字钟电路_1_out_16 ), .in_3(in_5),
    .out_12(\多功能数字钟电路_1_out_12 ), .out_13(\多功能数字钟电路_1_out_13 ), .out_14(\多功能数字钟电路_1_out_14 ),
    .out_15(\多功能数字钟电路_1_out_15 ), .out_17(\多功能数字钟电路_1_out_17 ), .out_18(\多功能数字钟电路_1_out_18 ),
    .out_11(\多功能数字钟电路_1_out_11 ), .out_8(\多功能数字钟电路_1_out_8 ), .out_9(\多功能数字钟电路_1_out_9 ),
    .out_10(\多功能数字钟电路_1_out_10 ), .in_1(clock_1_out));
  Hex_Digit_Display hex_digit_display_5 (.value(\多功能数字钟电路_1_out_12 ));  // open: dp
  LED #(.active("true")) led_1 (.in(\多功能数字钟电路_1_out_16 ));
  Hex_Digit_Display hex_digit_display_6 (.value(\多功能数字钟电路_1_out_13 ));  // open: dp
endmodule

module \转换1  (
  input  [7:0] in_1,
  output [7:0] out_2
);

  wire comparator_1_eq, comparator_2_eq;
  wire [7:0] multiplexer_1_out;

  Multiplexer #(.select(1), .width(8), .disabled("Z"), .enable("false")) multiplexer_1 (
    .in0(in_1), .in1(8'h20), .out(multiplexer_1_out), .sel(comparator_1_eq));
  Comparator #(.width(8), .mode("twosComplement")) comparator_1 (
    .a(in_1), .b(8'h1a), .eq(comparator_1_eq));  // open: gt, lt
  Multiplexer #(.select(1), .width(8), .disabled("Z"), .enable("false")) multiplexer_2 (
    .in0(multiplexer_1_out), .in1(8'h21), .out(out_2), .sel(comparator_2_eq));
  Comparator #(.width(8), .mode("twosComplement")) comparator_2 (
    .a(multiplexer_1_out), .b(8'h1b), .eq(comparator_2_eq));  // open: gt, lt
endmodule
